// Logisim project registerFile2_YousefAhmadzai.circ as structural Verilog: 1 circuit, main circuit main
module main (
);

  wire clock_1_out, decoder_1_out1, decoder_1_out3, decoder_1_out5, decoder_1_out6, decoder_1_out7, or_1_out;
  wire [7:0] ACC_q, adder_3_out, multiplexer_2_out, ram_1_data, ram_2_data, ram_2_data_2;
  wire [15:0] adder_1_out, adder_2_out, bit_extender_1_out, multiplexer_1_out, register_1_q;

  Register #(.width(16)) register_1 (.D(multiplexer_1_out), .en(1'b1), .Q(register_1_q), .clk(clock_1_out), .clr(1'b0));
  Clock clock_1 (.out(clock_1_out));
  Multiplexer #(.width(16), .enable("false")) multiplexer_1 (
    .in0(adder_1_out), .in1(adder_2_out), .out(multiplexer_1_out), .sel(decoder_1_out6));
  Register ACC (.D(adder_3_out), .en(or_1_out), .Q(ACC_q), .clk(clock_1_out));  // open: clr
  // Probe on ACC_q
  Adder #(.width(16)) adder_1 (.a(register_1_q), .b(16'h1), .out(adder_1_out));  // open: cin, cout
  RAM #(.addrWidth(3), .bus("separate")) ram_1 (
    .addr(ram_2_data[5:3]), .din(ACC_q), .data(ram_1_data), .str(decoder_1_out7), .sel(1'b1),
    .clk(clock_1_out), .clr(1'b0));  // open: ld
  // Probe on ram_1_data
  or or_1 (or_1_out, decoder_1_out1, decoder_1_out3);
  Adder #(.width(16)) adder_2 (.a(bit_extender_1_out), .b(register_1_q), .out(adder_2_out));  // open: cin, cout
  Adder adder_3 (.a(ram_1_data), .b(multiplexer_2_out), .out(adder_3_out));  // open: cin, cout
  // Probe on multiplexer_2_out
  Multiplexer #(.width(8), .enable("false")) multiplexer_2 (
    .in0(ram_2_data_2), .in1(ACC_q), .out(multiplexer_2_out), .sel(decoder_1_out1));
  // Probe on adder_3_out
  assign bit_extender_1_out = {{8{ram_2_data_2[7]}}, ram_2_data_2};  // Bit_Extender bit_extender_1
  RAM #(.addrWidth(16), .dataWidth(16), .bus("separate")) ram_2 (
    .addr(register_1_q), .data({ram_2_data_2, ram_2_data}), .str(1'b0), .sel(1'b1), .clk(clock_1_out),
    .clr(1'b0));  // open: din, ld
  TTY tty_1 (.data(ram_2_data_2[6:0]), .clk(clock_1_out), .we(decoder_1_out5), .clr(1'b0));
  Decoder #(.select(3), .enable("false")) decoder_1 (
    .out1(decoder_1_out1), .out3(decoder_1_out3), .out5(decoder_1_out5), .out6(decoder_1_out6),
    .out7(decoder_1_out7), .sel(ram_2_data[2:0]));  // open: out0, out2, out4

  // Notes on the sheet:
  //   Register File
  //   SIX = jump (my six key doesnt work so i typed six)
  //   5 = tty print
  //   3 = reg add
endmodule
